// Digital circuit register-file.dig as structural Verilog
module register_file (
  input  [4:0] ReadReg1,
  input  [4:0] ReadReg2,
  input  [4:0] WriteReg,
  input  [31:0] WriteData,
  input  RegWrite,
  input  Clock,
  output [31:0] ReadData1,
  output [31:0] ReadData2
);

  wire writ0, writ1, writ2, writ3, writ4, writ5, writ6, writ7, writ8, writ9, writ10, writ11, writ12, writ13,
       writ14, writ15, writ16, writ17, writ18, writ19, writ20, writ21, writ22, writ23, writ24, writ25,
       writ26, writ27, writ28, writ29, writ30, writ31, write0, write1, write2, write3, write4, write5,
       write6, write7, write8, write9, write10, write11, write12, write13, write14, write15, write16,
       write17, write18, write19, write20, write21, write22, write23, write24, write25, write26, write27,
       write28, write29, write30, write31;
  wire [31:0] r0, r1, r2, r3, r4, r5, r6, r7, r8, r9, r10, r11, r12, r13, r14, r15, r16, r17, r18, r19, r20,
       r21, r22, r23, r24, r25, r26, r27, r28, r29, r30, r31;

  Register #(.Bits(32)) Register_0 (.D(WriteData), .C(Clock), .en(write0), .Q(r0));
  Register #(.Bits(32)) Register_1 (.D(WriteData), .C(Clock), .en(write1), .Q(r1));
  Register #(.Bits(32)) Register_2 (.D(WriteData), .C(Clock), .en(write2), .Q(r2));
  Register #(.Bits(32)) Register_3 (.D(WriteData), .C(Clock), .en(write3), .Q(r3));
  Register #(.Bits(32)) Register_4 (.D(WriteData), .C(Clock), .en(write4), .Q(r4));
  Register #(.Bits(32)) Register_15 (.D(WriteData), .C(Clock), .en(write15), .Q(r15));
  Register #(.Bits(32)) Register_16 (.D(WriteData), .C(Clock), .en(write16), .Q(r16));
  Register #(.Bits(32)) Register_17 (.D(WriteData), .C(Clock), .en(write17), .Q(r17));
  Register #(.Bits(32)) Register_18 (.D(WriteData), .C(Clock), .en(write18), .Q(r18));
  Register #(.Bits(32)) Register_19 (.D(WriteData), .C(Clock), .en(write19), .Q(r19));
  Register #(.Bits(32)) Register_5 (.D(WriteData), .C(Clock), .en(write5), .Q(r5));
  Register #(.Bits(32)) Register_6 (.D(WriteData), .C(Clock), .en(write6), .Q(r6));
  Register #(.Bits(32)) Register_7 (.D(WriteData), .C(Clock), .en(write7), .Q(r7));
  Register #(.Bits(32)) Register_8 (.D(WriteData), .C(Clock), .en(write8), .Q(r8));
  Register #(.Bits(32)) Register_9 (.D(WriteData), .C(Clock), .en(write9), .Q(r9));
  Register #(.Bits(32)) Register_20 (.D(WriteData), .C(Clock), .en(write20), .Q(r20));
  Register #(.Bits(32)) Register_21 (.D(WriteData), .C(Clock), .en(write21), .Q(r21));
  Register #(.Bits(32)) Register_22 (.D(WriteData), .C(Clock), .en(write22), .Q(r22));
  Register #(.Bits(32)) Register_23 (.D(WriteData), .C(Clock), .en(write23), .Q(r23));
  Register #(.Bits(32)) Register_24 (.D(WriteData), .C(Clock), .en(write24), .Q(r24));
  Register #(.Bits(32)) Register_10 (.D(WriteData), .C(Clock), .en(write10), .Q(r10));
  Register #(.Bits(32)) Register_11 (.D(WriteData), .C(Clock), .en(write11), .Q(r11));
  Register #(.Bits(32)) Register_12 (.D(WriteData), .C(Clock), .en(write12), .Q(r12));
  Register #(.Bits(32)) Register_13 (.D(WriteData), .C(Clock), .en(write13), .Q(r13));
  Register #(.Bits(32)) Register_14 (.D(WriteData), .C(Clock), .en(write14), .Q(r14));
  Register #(.Bits(32)) Register_25 (.D(WriteData), .C(Clock), .en(write25), .Q(r25));
  Register #(.Bits(32)) Register_26 (.D(WriteData), .C(Clock), .en(write26), .Q(r26));
  Register #(.Bits(32)) Register_27 (.D(WriteData), .C(Clock), .en(write27), .Q(r27));
  Register #(.Bits(32)) Register_28 (.D(WriteData), .C(Clock), .en(write28), .Q(r28));
  Register #(.Bits(32)) Register_29 (.D(WriteData), .C(Clock), .en(write29), .Q(r29));
  Register #(.Bits(32)) Register_30 (.D(WriteData), .C(Clock), .en(write30), .Q(r30));
  Register #(.Bits(32)) Register_31 (.D(WriteData), .C(Clock), .en(write31), .Q(r31));
  Decoder #(.Selector_Bits(5)) decoder_1 (
    .sel(WriteReg), .out_0(writ0), .out_1(writ1), .out_2(writ2), .out_3(writ3), .out_4(writ4), .out_5(writ5),
    .out_6(writ6), .out_7(writ7), .out_8(writ8), .out_9(writ9), .out_10(writ10), .out_11(writ11),
    .out_12(writ12), .out_13(writ13), .out_14(writ14), .out_15(writ15), .out_16(writ16), .out_17(writ17),
    .out_18(writ18), .out_19(writ19), .out_20(writ20), .out_21(writ21), .out_22(writ22), .out_23(writ23),
    .out_24(writ24), .out_25(writ25), .out_26(writ26), .out_27(writ27), .out_28(writ28), .out_29(writ29),
    .out_30(writ30), .out_31(writ31));
  and and_1 (write0, writ0, RegWrite);
  and and_2 (write1, writ1, RegWrite);
  and and_3 (write2, writ2, RegWrite);
  and and_4 (write3, writ3, RegWrite);
  and and_5 (write4, writ4, RegWrite);
  and and_6 (write5, writ5, RegWrite);
  and and_7 (write6, writ6, RegWrite);
  Multiplexer #(.Bits(32), .Selector_Bits(5)) multiplexer_1 (
    .sel(ReadReg1), .in_0(r0), .in_1(r1), .in_2(r2), .in_3(r3), .in_4(r4), .in_5(r5), .in_6(r6), .in_7(r7),
    .in_8(r8), .in_9(r9), .in_10(r10), .in_11(r11), .in_12(r12), .in_13(r13), .in_14(r14), .in_15(r15),
    .in_16(r16), .in_17(r17), .in_18(r18), .in_19(r19), .in_20(r20), .in_21(r21), .in_22(r22), .in_23(r23),
    .in_24(r24), .in_25(r25), .in_26(r26), .in_27(r27), .in_28(r28), .in_29(r29), .in_30(r30), .in_31(r31),
    .out(ReadData1));
  and and_8 (write7, writ7, RegWrite);
  and and_9 (write8, writ8, RegWrite);
  and and_10 (write9, writ9, RegWrite);
  and and_11 (write10, writ10, RegWrite);
  and and_12 (write11, writ11, RegWrite);
  and and_13 (write12, writ12, RegWrite);
  and and_14 (write13, writ13, RegWrite);
  Multiplexer #(.Selector_Bits(5), .Bits(32)) multiplexer_2 (
    .sel(ReadReg2), .in_0(r0), .in_1(r1), .in_2(r2), .in_3(r3), .in_4(r4), .in_5(r5), .in_6(r6), .in_7(r7),
    .in_8(r8), .in_9(r9), .in_10(r10), .in_11(r11), .in_12(r12), .in_13(r13), .in_14(r14), .in_15(r15),
    .in_16(r16), .in_17(r17), .in_18(r18), .in_19(r19), .in_20(r20), .in_21(r21), .in_22(r22), .in_23(r23),
    .in_24(r24), .in_25(r25), .in_26(r26), .in_27(r27), .in_28(r28), .in_29(r29), .in_30(r30), .in_31(r31),
    .out(ReadData2));
  and and_15 (write14, writ14, RegWrite);
  and and_16 (write15, writ15, RegWrite);
  and and_17 (write16, writ16, RegWrite);
  and and_18 (write17, writ17, RegWrite);
  and and_19 (write18, writ18, RegWrite);
  and and_20 (write19, writ19, RegWrite);
  and and_21 (write20, writ20, RegWrite);
  and and_22 (write21, writ21, RegWrite);
  and and_23 (write22, writ22, RegWrite);
  and and_24 (write23, writ23, RegWrite);
  and and_25 (write24, writ24, RegWrite);
  and and_26 (write25, writ25, RegWrite);
  and and_27 (write26, writ26, RegWrite);
  and and_28 (write27, writ27, RegWrite);
  and and_29 (write28, writ28, RegWrite);
  and and_30 (write29, writ29, RegWrite);
  and and_31 (write30, writ30, RegWrite);
  and and_32 (write31, writ31, RegWrite);
endmodule

/* Test case Register File Test:
WriteReg WriteData RegWrite Clock ReadReg1 ReadReg2 ReadData1 ReadData2

# $1 = 25
1 25 1 C 1 0 25 0

# $2 = 30
2 30 1 C 0 2 0 30

# $(N+1) = (N+1)
loop(N, 30)
	(N+1) (N+1) 1 C (N+1) (N) (N+1) (N)
end loop

# $(N+1) = N-60
loop(N, 30)
	(N+1) (N-60) 1 C (N+1) (N+1) (N-60) (N-60)
end loop

# Try writing to $0. This should not write anything
0 25 1 C 0 0 0 0

# try writing when RegWrite = 0
# (the registers should still have their old values)
loop(N, 30)
	(N+1) (N+80) 0 C (N+1) (N+1) (N-60) (N-60)
end loop
*/
