// Digital circuit control-unit.dig as structural Verilog
module control_unit (
  input  [6:0] opcode,
  input  [2:0] funct3,
  input  [6:0] funct7,
  output RegWrite,
  output ALUSrc,
  output ImmSrc1,
  output ImmSrc0,
  output ALUOp3,
  output ALUOp2,
  output ALUOp1,
  output ALUOp0
);

  wire comparator_1_eq, comparator_2_eq, comparator_3_eq, comparator_4_eq, comparator_5_eq, comparator_6_eq,
       comparator_7_eq, comparator_8_eq, comparator_9_eq, comparator_10_eq, comparator_11_eq,
       comparator_12_eq, comparator_13_eq, comparator_14_eq, comparator_15_eq, comparator_16_eq,
       comparator_17_eq, comparator_18_eq, comparator_19_eq, comparator_20_eq, comparator_21_eq, is_add,
       is_addi, is_and, is_andi, is_or, is_slt, is_slti, is_sub;
  wire [2:0] rom_addr;

  PriorityEncoder #(.Selector_Bits(3)) priorityencoder_1 (
    .in0(is_add), .in1(is_sub), .in2(is_and), .in3(is_or), .in4(is_slt), .in5(is_addi), .in6(is_slti),
    .in7(is_andi), .num(rom_addr));  // open: any
  ROM #(.AddrBits(3), .Bits(8)) controlUnitRom (
    .A(rom_addr), .sel(1'b1), .D({RegWrite, ALUSrc, ImmSrc1, ImmSrc0, ALUOp3, ALUOp2, ALUOp1, ALUOp0}));
  Comparator #(.Bits(7)) comparator_1 (.a({7{1'b0}}), .b(funct7), .eq(comparator_1_eq));  // open: gt, lt
  Comparator #(.Bits(3)) comparator_2 (.a(3'b000), .b(funct3), .eq(comparator_2_eq));  // open: gt, lt
  Comparator #(.Bits(7)) comparator_3 (.a(7'b0110011), .b(opcode), .eq(comparator_3_eq));  // open: gt, lt
  Comparator #(.Bits(7)) comparator_4 (.a({7{1'b0}}), .b(funct7), .eq(comparator_4_eq));  // open: gt, lt
  Comparator #(.Bits(3)) comparator_5 (.a(3'b111), .b(funct3), .eq(comparator_5_eq));  // open: gt, lt
  Comparator #(.Bits(7)) comparator_6 (.a(7'b0110011), .b(opcode), .eq(comparator_6_eq));  // open: gt, lt
  Comparator #(.Bits(7)) comparator_7 (.a({7{1'b0}}), .b(funct7), .eq(comparator_7_eq));  // open: gt, lt
  Comparator #(.Bits(3)) comparator_8 (.a(3'b010), .b(funct3), .eq(comparator_8_eq));  // open: gt, lt
  Comparator #(.Bits(7)) comparator_9 (.a(7'b0110011), .b(opcode), .eq(comparator_9_eq));  // open: gt, lt
  Comparator #(.Bits(3)) comparator_10 (.a(3'b010), .b(funct3), .eq(comparator_10_eq));  // open: gt, lt
  Comparator #(.Bits(7)) comparator_11 (.a(7'b0010011), .b(opcode), .eq(comparator_11_eq));  // open: gt, lt
  and and_1 (is_add, comparator_1_eq, comparator_2_eq, comparator_3_eq);
  and and_2 (is_and, comparator_4_eq, comparator_5_eq, comparator_6_eq);
  and and_3 (is_slt, comparator_7_eq, comparator_8_eq, comparator_9_eq);
  and and_4 (is_slti, comparator_10_eq, comparator_11_eq);
  Comparator #(.Bits(7)) comparator_12 (.a(7'b0100000), .b(funct7), .eq(comparator_12_eq));  // open: gt, lt
  Comparator #(.Bits(3)) comparator_13 (.a(3'b000), .b(funct3), .eq(comparator_13_eq));  // open: gt, lt
  Comparator #(.Bits(7)) comparator_14 (.a(7'b0110011), .b(opcode), .eq(comparator_14_eq));  // open: gt, lt
  Comparator #(.Bits(7)) comparator_15 (.a({7{1'b0}}), .b(funct7), .eq(comparator_15_eq));  // open: gt, lt
  Comparator #(.Bits(3)) comparator_16 (.a(3'b110), .b(funct3), .eq(comparator_16_eq));  // open: gt, lt
  Comparator #(.Bits(7)) comparator_17 (.a(7'b0110011), .b(opcode), .eq(comparator_17_eq));  // open: gt, lt
  Comparator #(.Bits(3)) comparator_18 (.a(3'b000), .b(funct3), .eq(comparator_18_eq));  // open: gt, lt
  Comparator #(.Bits(7)) comparator_19 (.a(7'b0010011), .b(opcode), .eq(comparator_19_eq));  // open: gt, lt
  Comparator #(.Bits(3)) comparator_20 (.a(3'b111), .b(funct3), .eq(comparator_20_eq));  // open: gt, lt
  Comparator #(.Bits(7)) comparator_21 (.a(7'b0010011), .b(opcode), .eq(comparator_21_eq));  // open: gt, lt
  and and_5 (is_sub, comparator_12_eq, comparator_13_eq, comparator_14_eq);
  and and_6 (is_or, comparator_15_eq, comparator_16_eq, comparator_17_eq);
  and and_7 (is_addi, comparator_18_eq, comparator_19_eq);
  and and_8 (is_andi, comparator_20_eq, comparator_21_eq);

  // Notes on the sheet:
  //   contents of controlUnitRom (hex, n*v repeats v):
  //   82,86,80,81,87,c2,c7,c0
endmodule
